# Fritzing sketch jetson_finder_schmetics (saved by Fritzing 0.9.4)
breadboards: 1

parts:
  Jetson_Nano2 = Jetson Nano
  R1 = Resistor [tolerance=±5% resistance=220 package=THT]
  LED1 = RGB LED (com. cathode, rgb) [package="5 mm [THT]"]
  R2 = Rotary Potentiometer (Small) [maximum_resistance=100kΩ package=THT]
  R3 = Resistor [tolerance=±5% resistance=220 package=THT]
  R4 = Resistor [tolerance=±5% resistance=220 package=THT]
  Parça1 = Arduino Uno (Rev3)  # not connected
  Parça2 = Arduino Uno (Rev3)

nets:
  N1: Jetson_Nano2.GPIO9, R2.leg2
  N2: Jetson_Nano2.GPIO8, R2.leg1
  N3: Jetson_Nano2.GPIO24, Parça2.D3_PWM
  N4: Jetson_Nano2.GPIO18, R4.Pin_1
  N5: Jetson_Nano2.GPIO15, R3.Pin_1
  N6: Jetson_Nano2.GPIO14, R1.Pin_1
  N7: Jetson_Nano2.GND, Parça2.D2
  N8: Jetson_Nano2.5V, LED1.common_cathode
  N9: R1.Pin_0, LED1.blue_anode
  N10: LED1.red_anode, R4.Pin_0
  N11: LED1.green_anode, R3.Pin_0
  N12: R2.wiper, Parça2.A0
